# Fritzing sketch server-ble (saved by Fritzing 0.9.5d)
breadboards: 2

parts:
  M1 = DOIT Esp32 DevKit v1 (30 pins long, 11 pins width) [part_number=ESP32S-PIN30]
  Part2 = Arduino Nano (Rev3.0) (ICSP)  # not connected
  Part3 = TXB0108 8-channel Bi-directional Logic Level Converter
  YwRobot_Power_Supply1 = YwRobot Breadboard Power Supply [part_number=545043]
  LCD2004-I2C1 = LCD2004-I2C  # not connected
  M2 = Stepper Motor - 8 wire  # not connected
  Part4 = KY-033 Tracing Black White Line Hunting Sensor Module For Arduino  # not connected

nets:
  N1: M1.3V3, Part3.VCCA
  N2: M1.GND, YwRobot_Power_Supply1.GND#13, YwRobot_Power_Supply1.GND#14
  N3: M1.D23, Part3.OE
  N4: M1.VIN, YwRobot_Power_Supply1.VCC#5, YwRobot_Power_Supply1.VCC#6
  N5: Part3.GND, YwRobot_Power_Supply1.GND#11, YwRobot_Power_Supply1.GND#12
  N6: YwRobot_Power_Supply1.VCC#9, YwRobot_Power_Supply1.VCC#10

custom parts:
  DOIT Esp32 DevKit v1 (30 pins long, 11 pins width): The DOIT Esp32 DevKit v1 is one of the development board created by DOIT to evaluate the ESP-WROOM-32 module. It is based on the ESP32 microcontroller that boasts Wifi, Bluetooth, Ethernet and Low Power support all in a single chip. (vanepp) made breadboard work, adjusted pin numbering and labels and reduced size of schematic and cleaned up pcb. This chip is 30pins long (2 x15) and 11 pins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
  TXB0108 8-channel Bi-directional Logic Level Converter: Because the Arduino (and Basic Stamp) are 5V devices, and most modern sensors, displays, flash cards and modes are 3.3V-only, many makers find that they need to perform level shifting/conversion to protect the 3.3V device from 5V. Although one can use resistors to make a divider, for high speed transfers, the resistors can add a lot of slew and cause havoc that is tough to debug. For that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
  YwRobot Breadboard Power Supply: The YwRobot Breadboard Power Supply (MB-V2) has two power rails; they can be 5V or 3V3. Power to the module can be provided through the female USB socket or through the A10 (female) 2.1mm power jack.
  LCD2004-I2C: A standard character display with 4x20 characters. Comes in many colors with LCM2004 IIC attached.
  Stepper Motor - 8 wire: Simple, but very powerful bi polar stepper motor. 8 wire
  KY-033 Tracing Black White Line Hunting Sensor Module For Arduino: Tracing Black White Line Hunting Sensor Module For Arduino Description: This is KY-033 tracking sensor. The KY-033 measures the intensity of infrared radiation and delivers it as an analog output voltage. Features: Operating voltage: 2.5 - 12V(cannot over12V) working current: 18mA-20mA at 5V Enhanced accuracy Documents: http://www.vishay.com/docs/83760/tcrt5000.pdf
